# Fritzing sketch NES-controller-IN (saved by Fritzing 0.9.2b)
circuit board: 8.46667cm x 5.64444cm
breadboards: 1

parts:
  Pro_Trinket_5V = Pro Trinket 5V
  To_NES_P4 = female pin header, 5 pins [form="♀ (female)"]
  To_Controller = female pin header, 5 pins [form="♀ (female)"]

nets:
  N1: Pro_Trinket_5V.VBAT, To_NES_P4.pin5, To_Controller.pin5
  N2: Pro_Trinket_5V.GND, To_NES_P4.pin1, To_Controller.pin1
  N3: Pro_Trinket_5V.D6, To_NES_P4.pin4, To_Controller.pin4
  N4: Pro_Trinket_5V.D5, To_NES_P4.pin2, To_Controller.pin2
  N5: Pro_Trinket_5V.D3, To_NES_P4.pin3, To_Controller.pin3

custom parts:
  Pro Trinket 5V: The Pro Trinket 5V is like an Arduino Pro Mini with more pins and USB included. Built with the common core Arduino chip, the ATmega328p, it has 18 GPIO, 2 extra analog inputs, 28K of flash, and 2K of RAM. It has onboard USB bootloading support with Optiboot support, so you can either program your Pro Trinket over USB or with a FTDI cable. The Pro Trinket is programmable using the Arduino IDE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

// code stored in the sketch: NES-controller-IN.ino
//This sketch will allow your arduino to output whatever inputs you give your NES
//  Serial ouput at 9600 is a time stamped list of input changes
//  Connect all inputs as taps to the existing data, the arduino just listens.
//  It could probably be modified to create output that is then fed back in, but this script does not do that.

//Some ref(but not the initial idea):
//    https://github.com/mattpbooth/ArduinoNESController 

//Pins
// I'm using a Pro Trinket 5V for this dev work
#define LATCH   3
#define CLOCK   5
#define DATA    6

//because I want to define stuff clearer:
#define NONE      0b00000000
#define RIGHT     0b00000001
#define LEFT      0b00000010
#define DOWN      0b00000100
#define UP        0b00001000
#define START     0b00010000
#define SELECT    0b00100000
#define BUTTONB   0b01000000
#define BUTTONA   0b10000000

//I don't like magic numbers, but for now I need this, at least until I come up with a better read process.
#define MAGIC   3   //made this up as I went... it's to give time for the clock to go low

//aparently this needs to be volatile due to being changed in an interrupt:
//    https://www.arduino.cc/en/Reference/Volatile
volatile byte controller = 0;
byte last = 0;

void setup() {
  //First we setup serial for debug/input as needed.
  Serial.begin(9600);
  Serial.println("NES Online:");

  //Setup the CLOCK and DATA pins as input
  pinMode(CLOCK, INPUT);
  pinMode(DATA, INPUT);

  //Link pin LATCH as an interupt input
  pinMode(LATCH, INPUT);
  //Trigger only when the pin falls low: FALLING
  attachInterrupt(digitalPinToInterrupt(LATCH), latchIN, FALLING);
  //see: https://www.arduino.cc/en/Reference/AttachInterrupt 
}

void loop() {
  if (last != controller) {
    /*Serial.print(millis());
    Serial.print(": B: ");
    Serial.print(controller, BIN);
    Serial.print(": D: ");
    Serial.println(controller);*/

    Serial.print(millis());
    Serial.print(": ");
    if (controller & LEFT)    Serial.print("LEFT   : "); else Serial.print("       : ");
    if (controller & RIGHT)   Serial.print("RIGHT  : "); else Serial.print("       : ");
    if (controller & UP)      Serial.print("UP     : "); else Serial.print("       : ");
    if (controller & DOWN)    Serial.print("DOWN   : "); else Serial.print("       : ");
    if (controller & BUTTONA) Serial.print("A      : "); else Serial.print("       : ");
    if (controller & BUTTONB) Serial.print("B      : "); else Serial.print("       : ");
    if (controller & START)   Serial.print("START  : "); else Serial.print("       : ");
    if (controller & SELECT)  Serial.print("SELECT : "); else Serial.print("       : ");
    if (controller == 0 )     Serial.print("NONE   : "); else Serial.print("       : ");
    
    Serial.print(": 0x");
    Serial.print(controller, HEX);
    Serial.print(": D: ");
    Serial.print(controller);
    
    Serial.println("");
    
    last = controller;
  }
  //delay(500);
}

//Read the state of the controller and store it.
//    http://www.mit.edu/~tarvizo/nes-controller.html
void latchIN() {
  //store the controller state internally first
  byte input = 0;

  // we waited for the latch to fall before calling the interrupt so that we can read the first bit now
  //    we would have to wait for LATCH to go low otherwise, here
  
  //read 8 bits on the clock
  for (int i = 7; i >= 0; i--) {
    //pull the status of the DATA pin and shift it over to match position of the bit
    //the value is active low, so we should get all 1's when nothing is happening
    input += digitalRead(DATA) << i;

    //delay a bit after this, in theory we should do a digital read until low,
    //    but it's too slow and causes big issues
    //This magic number was found experimentally, and technically could cause problems if the game
    //    uses a non-standard timing to read the state, which is allowed. Most games should get the
    //    controller state as fast as possible, so I suspect this will be fine for now
    //TODO: resolve this somehow - I do get spurious data sometimes due to this flaw
    delayMicroseconds(MAGIC); 
    //wait for the clock to go back low, so we don't read the next bit instantly
    while(digitalRead(CLOCK) != HIGH) {}
  }

  // we assign the value to the global, but inverted so that 1 is pressed, and 0 is not
  controller = ~input;
}
